// Logisim project Control Unit.circ as structural Verilog: 1 circuit, main circuit main
module main (
  input  [31:0] Instruction,
  output [5:0] OP_Code,
  output RegDes,
  output ALUsrc,
  output RegWrite,
  output jump,
  output branch,
  output MemWrite,
  output MemRead,
  output MemToReg,
  output ExOp
);

  wire addi_out, andi_out, divi_out, muli_out, ori_out, subi_out;

  and addi (addi_out, ~Instruction[26], Instruction[27], Instruction[28], ~Instruction[29], ~Instruction[30]);  // AND_Gate
  and subi (subi_out, Instruction[26], Instruction[27], Instruction[28], ~Instruction[29], ~Instruction[30]);  // AND_Gate
  and muli (muli_out, ~Instruction[26], ~Instruction[27], ~Instruction[28], Instruction[29], ~Instruction[30]);  // AND_Gate
  and divi (divi_out, Instruction[26], ~Instruction[27], ~Instruction[28], Instruction[29], ~Instruction[30]);  // AND_Gate
  and ori (ori_out, ~Instruction[26], Instruction[27], ~Instruction[28], Instruction[29], ~Instruction[30]);  // AND_Gate
  and andi (andi_out, Instruction[26], Instruction[27], ~Instruction[28], Instruction[29], ~Instruction[30]);  // AND_Gate
  and lw (MemRead, ~Instruction[26], ~Instruction[27], Instruction[28], Instruction[29], ~Instruction[30]);  // AND_Gate
  and sw (MemWrite, Instruction[26], ~Instruction[27], Instruction[28], Instruction[29], ~Instruction[30]);  // AND_Gate
  and beq (branch, ~Instruction[26], Instruction[27], Instruction[28], Instruction[29], ~Instruction[30]);  // AND_Gate
  and u_jump (jump, Instruction[26], Instruction[27], Instruction[28], Instruction[29], ~Instruction[30]);  // AND_Gate
  or or_1 (ALUsrc, MemWrite, MemRead, andi_out, ori_out, divi_out, muli_out, subi_out, addi_out);
  or or_2 (RegWrite, Instruction[31], MemRead, andi_out, ori_out, divi_out, muli_out, subi_out, addi_out);
  or or_3 (MemToReg, MemRead, branch);
  or or_4 (ExOp, Instruction[31], MemWrite, MemRead, branch);

  assign OP_Code = Instruction[31:26];
  assign RegDes = Instruction[31];
endmodule
